# Fritzing sketch esp32-led-matrix (saved by Fritzing 0.9.3b)

parts:
  U1 = ESP 32 DEVKIT DOIT
  Part1 = Matrix LED de 8x8 basada en MAX7219

nets:
  N1: U1.D22, U1.D5, U1.D4, U1.D2, Part1.CS, Part1.CLK, Part1.DIN
  VIN: U1.VIN, Part1.VCC
  GND: U1.GND, Part1.GND
